// Logisim project main.circ as structural Verilog: 6 circuits, main circuit main
module main (
);

  wire cdm_8_1_p2, cdm_8_1_p4, cdm_8_1_p5, cdm_8_1_p6, cdm_8_1_p7, cdm_8_1_p8, cdm_8_1_p9, cdm_8_1_p10, Cl,
       code, data, decoder_1_out0, decoder_2_out0, decoder_3_out0, decoder_4_out0, decoder_6_out0,
       decoder_7_out0, DN_out, FA_out, FB_out, FC_out, FD_out, FE_out, FF_out, I_Osel, In_out_prime, mem,
       nand_1_out, not_1_out, not_2_out, RAM, Rset, UP_out;
  wire [1:0] joystick_1_y;
  wire [2:0] register_3_q, register_4_q, register_5_q;
  wire [3:0] I_Oadr, LsIn, RsIn;
  wire [4:0] ballX, ballY, kinematic_controller_1_ballx_2, kinematic_controller_1_bally_2,
       kinematic_controller_1_chipid, rBat;
  wire [7:0] cdm_8_1_p14, cdm_8_1_p15, I_Odat, lBatOut;
  wire [7:4] cdm_8_1_p13, register_1_q, register_2_q;
  wire [31:0] kinematic_controller_1_leftbaty, kinematic_controller_1_rightbaty, n32cells_1_out_6,
       n32cells_1_out_7, n32cells_1_out_8, n32cells_1_out_9, n32cells_1_out_10, n32cells_1_out_11,
       n32cells_1_out_12, n32cells_1_out_13, n32cells_1_out_14, n32cells_1_out_15, n32cells_1_out_16,
       n32cells_1_out_17, n32cells_1_out_18, n32cells_1_out_19, n32cells_1_out_20, n32cells_1_out_21,
       n32cells_1_out_22, n32cells_1_out_23, n32cells_1_out_24, n32cells_1_out_25, n32cells_1_out_26,
       n32cells_1_out_27, n32cells_1_out_28, n32cells_1_out_29, n32cells_1_out_30, n32cells_1_out_31,
       n32cells_1_out_32, n32cells_1_out_33, n32cells_1_out_34, n32cells_1_out_35, n32cells_1_out_36,
       n32cells_1_out_37;

  Hex_Digit_Display hex_digit_display_1 (.value(LsIn));  // open: dp
  Button UP (.out(UP_out));
  Button DN (.out(DN_out));
  // Probe on I_Odat
  // Probe on I_Oadr
  Register register_1 (.D(I_Odat), .Q({register_1_q, LsIn}), .clk(decoder_1_out0));  // open: en, clr
  Hex_Digit_Display hex_digit_display_2 (.value(LsIn));  // open: dp
  // Probe on joystick_1_y
  Joystick #(.bits(2)) joystick_1 (.y(joystick_1_y));  // open: x
  Button R (.out(Rset));
  DotMatrix #(.matrixcols(32), .matrixrows(32)) dotmatrix_1 (
    .col0(n32cells_1_out_6), .col1(n32cells_1_out_22), .col2(n32cells_1_out_7), .col3(n32cells_1_out_23),
    .col4(n32cells_1_out_8), .col5(n32cells_1_out_24), .col6(n32cells_1_out_9), .col7(n32cells_1_out_25),
    .col8(n32cells_1_out_10), .col9(n32cells_1_out_26), .col10(n32cells_1_out_11), .col11(n32cells_1_out_27),
    .col12(n32cells_1_out_12), .col13(n32cells_1_out_28), .col14(n32cells_1_out_13),
    .col15(n32cells_1_out_29), .col16(n32cells_1_out_14), .col17(n32cells_1_out_30),
    .col18(n32cells_1_out_15), .col19(n32cells_1_out_31), .col20(n32cells_1_out_16),
    .col21(n32cells_1_out_32), .col22(n32cells_1_out_17), .col23(n32cells_1_out_33),
    .col24(n32cells_1_out_18), .col25(n32cells_1_out_34), .col26(n32cells_1_out_19),
    .col27(n32cells_1_out_35), .col28(n32cells_1_out_20), .col29(n32cells_1_out_36),
    .col30(n32cells_1_out_21), .col31(n32cells_1_out_37));
  _32cells u_32cells_1 (
    .chipID(kinematic_controller_1_chipid), .ballX(kinematic_controller_1_ballx_2),
    .ballY(kinematic_controller_1_bally_2), .leftbatY(kinematic_controller_1_leftbaty),
    .rightbatY(kinematic_controller_1_rightbaty), .out_6(n32cells_1_out_6), .out_22(n32cells_1_out_22),
    .out_7(n32cells_1_out_7), .out_23(n32cells_1_out_23), .out_8(n32cells_1_out_8),
    .out_24(n32cells_1_out_24), .out_9(n32cells_1_out_9), .out_25(n32cells_1_out_25),
    .out_10(n32cells_1_out_10), .out_26(n32cells_1_out_26), .out_11(n32cells_1_out_11),
    .out_27(n32cells_1_out_27), .out_12(n32cells_1_out_12), .out_28(n32cells_1_out_28),
    .out_13(n32cells_1_out_13), .out_29(n32cells_1_out_29), .out_14(n32cells_1_out_14),
    .out_30(n32cells_1_out_30), .out_15(n32cells_1_out_15), .out_31(n32cells_1_out_31),
    .out_16(n32cells_1_out_16), .out_32(n32cells_1_out_32), .out_17(n32cells_1_out_17),
    .out_33(n32cells_1_out_33), .out_18(n32cells_1_out_18), .out_34(n32cells_1_out_34),
    .out_19(n32cells_1_out_19), .out_35(n32cells_1_out_35), .out_20(n32cells_1_out_20),
    .out_36(n32cells_1_out_36), .out_21(n32cells_1_out_21), .out_37(n32cells_1_out_37));
  kinematic_controller kinematic_controller_1 (
    .ballX(ballX), .ballY(ballY), .rightBat(rBat), .velocity({8{1'b0}}),
    .chipID(kinematic_controller_1_chipid), .ballX_2(kinematic_controller_1_ballx_2),
    .ballY_2(kinematic_controller_1_bally_2), .leftbatY(kinematic_controller_1_leftbaty),
    .rightbatY(kinematic_controller_1_rightbaty), .reset(Rset), .Rscores(RsIn), .clock(Cl), .Lscores(LsIn),
    .joystick(joystick_1_y), .up(UP_out), .down(DN_out));
  and FC (FC_out, I_Osel, ~I_Oadr[0], ~I_Oadr[1], I_Oadr[2], I_Oadr[3]);  // AND_Gate
  Decoder #(.disabled(0)) decoder_1 (.out0(decoder_1_out0), .sel(In_out_prime), .en(FC_out));  // open: out1
  Hex_Digit_Display hex_digit_display_3 (.value(RsIn));  // open: dp
  and FD (FD_out, I_Osel, I_Oadr[0], ~I_Oadr[1], I_Oadr[2], I_Oadr[3]);  // AND_Gate
  Register register_2 (.D(I_Odat), .Q({register_2_q, RsIn}), .clk(decoder_2_out0));  // open: en, clr
  Decoder #(.disabled(0)) decoder_2 (.out0(decoder_2_out0), .sel(In_out_prime), .en(FD_out));  // open: out1
  Hex_Digit_Display hex_digit_display_4 (.value(RsIn));  // open: dp
  // Probe on I_Odat
  Clock clock_1 (.out(Cl));
  and FE (FE_out, I_Osel, ~I_Oadr[0], I_Oadr[1], I_Oadr[2], I_Oadr[3]);  // AND_Gate
  Register register_3 (.D(I_Odat), .Q({ballX, register_3_q}), .clk(decoder_3_out0));  // open: en, clr
  // Probe on {ballX, register_3_q}
  // Probe on cdm_8_1_p4
  // Probe on cdm_8_1_p5
  // Probe on cdm_8_1_p2
  // Probe on cdm_8_1_p6
  Button button_1 (.out(Rset));
  and and_1 (I_Osel, not_1_out, Cl, data);
  Decoder #(.disabled(0)) decoder_3 (.out0(decoder_3_out0), .sel(In_out_prime), .en(FE_out));  // open: out1
  // Probe on ballX
  // Probe on cdm_8_1_p7
  // Probe on cdm_8_1_p8
  // Probe on cdm_8_1_p9
  // CdM_8 cdm_8_1: pin names not known; wires that end beside it: Cl, cdm_8_1_p2, Rset, cdm_8_1_p4, cdm_8_1_p5, cdm_8_1_p6, cdm_8_1_p7, cdm_8_1_p8, cdm_8_1_p9, cdm_8_1_p10, mem, In_out_prime, {cdm_8_1_p13, I_Oadr}, cdm_8_1_p14, cdm_8_1_p15
  not not_1 (not_1_out, nand_1_out);
  nand nand_1 (nand_1_out, cdm_8_1_p13[4], cdm_8_1_p13[5], cdm_8_1_p13[6], cdm_8_1_p13[7]);
  and and_2 (RAM, nand_1_out, data);
  and FF (FF_out, I_Osel, I_Oadr[0], I_Oadr[1], I_Oadr[2], I_Oadr[3]);
  Register register_4 (.D(I_Odat), .Q({ballY, register_4_q}), .clk(decoder_4_out0));  // open: en, clr
  assign I_Odat = not_2_out ? cdm_8_1_p14 : 8'bz;  // Controlled_Buffer controlled_buffer_1
  not not_2 (not_2_out, In_out_prime);
  assign cdm_8_1_p15 = In_out_prime ? I_Odat : 8'bz;  // Controlled_Buffer controlled_buffer_2
  Decoder #(.disabled(0)) decoder_4 (.out0(decoder_4_out0), .sel(In_out_prime), .en(FF_out));  // open: out1
  // Probe on ballY
  Decoder decoder_5 (.out0(code), .out1(data), .sel(cdm_8_1_p10), .en(mem));
  // Probe on {cdm_8_1_p13, I_Oadr}
  assign I_Odat = decoder_6_out0 ? lBatOut : 8'bz;  // Controlled_Buffer controlled_buffer_3
  Pull_Resistor pull_resistor_1 (.node(I_Oadr[0]));
  Pull_Resistor pull_resistor_2 (.node(I_Oadr[1]));
  Pull_Resistor pull_resistor_3 (.node(I_Oadr[2]));
  Pull_Resistor pull_resistor_4 (.node(I_Oadr[3]));
  Pull_Resistor pull_resistor_5 (.node(cdm_8_1_p13[4]));
  Pull_Resistor pull_resistor_6 (.node(cdm_8_1_p13[5]));
  Pull_Resistor pull_resistor_7 (.node(cdm_8_1_p13[6]));
  Pull_Resistor pull_resistor_8 (.node(cdm_8_1_p13[7]));
  and FA (FA_out, I_Osel, ~I_Oadr[0], I_Oadr[1], ~I_Oadr[2], I_Oadr[3]);  // AND_Gate
  Decoder #(.disabled(0)) decoder_6 (.out0(decoder_6_out0), .sel(In_out_prime), .en(FA_out));  // open: out1
  ROM rom_1 (.addr({cdm_8_1_p13, I_Oadr}), .data(I_Odat), .sel(code));
  RAM ram_1 (.addr({cdm_8_1_p13, I_Oadr}), .data(I_Odat), .sel(RAM), .clk(Cl), .ld(In_out_prime));  // open: clr
  Register register_5 (.D(I_Odat), .Q({rBat, register_5_q}), .clk(decoder_7_out0));  // open: en, clr
  and FB (FB_out, I_Osel, I_Oadr[0], I_Oadr[1], ~I_Oadr[2], I_Oadr[3]);  // AND_Gate
  Decoder #(.disabled(0)) decoder_7 (.out0(decoder_7_out0), .sel(In_out_prime), .en(FB_out));  // open: out1

  // Other names for the same wires on the sheet: rd_wr_prime = In_out_prime

  // Notes on the sheet:
  //   Left Score
  //   Right Score
  //   BallX
  //   BallY
  //   Left Bat
  //   instr memory
  //   contents of rom_1 (hex, n*v repeats v):
  //   d0 3 d1 e1 a4 d0 2 d1 e2 a4 ee 10 ee 20 ee e d1 0 d0 dc a1 d0 fc a1 d0 dd a1 d0 fd a1 ee 20 d0 de d1
  //   fb f5 a1 d2 fe a9 d0 df d1 fc f5 a1 d0 ff a1 ee 34 d0 da d2 db d1 fd f5 a1 a9 d0 f8 a1 ee e d0 de b0
  //   d1 5 71 e3 51 d1 fa 71 e8 57 ee 68 d0 dd d2 fd ee 5d d0 dc d2 fc ee 5d b1 8d d3 9 a1 a9 77 e0 a ee c
  //   d0 de b0 d1 10 71 e3 7b d1 ef 71 e8 77 ee b4 d0 fa ee 7f d0 fb ee 7f b0 d2 df ba d1 18 11 78 e2 8b
  //   ee b4 79 e9 90 ee b4 d1 ef 79 e2 aa d1 7 11 79 e9 a3 d1 f 11 79 e2 a3 ee aa d3 e6 bd 81 ad ee aa d0
  //   e0 b1 81 d2 f9 a9 a1 ee b4 d0 df b0 d1 8 d2 f7 71 e9 c3 72 e2 c3 ee ca d3 e6 be 82 ae ee ca d0 e1 b0
  //   d1 e2 b5 ee d2 d2 de bb d2 e0 ba a e0 de 1c ee df 3c d2 de a8 d2 df bb d2 e6 ba a e0 ee 1d ee ef 3d
  //   d2 df a9 d3 fe d2 ff ac a9 ee e d4 80 80 80
  //   data memory
  //   Right Bat
endmodule

module _32cells (
  input  [4:0] chipID,
  input  [4:0] ballX,
  input  [4:0] ballY,
  input  [31:0] leftbatY,
  input  [31:0] rightbatY,
  output [31:0] out_6,
  output [31:0] out_7,
  output [31:0] out_8,
  output [31:0] out_9,
  output [31:0] out_10,
  output [31:0] out_11,
  output [31:0] out_12,
  output [31:0] out_13,
  output [31:0] out_14,
  output [31:0] out_15,
  output [31:0] out_16,
  output [31:0] out_17,
  output [31:0] out_18,
  output [31:0] out_19,
  output [31:0] out_20,
  output [31:0] out_21,
  output [31:0] out_22,
  output [31:0] out_23,
  output [31:0] out_24,
  output [31:0] out_25,
  output [31:0] out_26,
  output [31:0] out_27,
  output [31:0] out_28,
  output [31:0] out_29,
  output [31:0] out_30,
  output [31:0] out_31,
  output [31:0] out_32,
  output [31:0] out_33,
  output [31:0] out_34,
  output [31:0] out_35,
  output [31:0] out_36,
  output [31:0] out_37
);

  wire [4:0] n8cells_1_ballx_2, n8cells_1_bally_2, n8cells_1_chipid_2, n8cells_2_ballx_2, n8cells_2_bally_2,
       n8cells_2_chipid_2, n8cells_3_ballx_2, n8cells_3_bally_2, n8cells_3_chipid_2;
  wire [31:0] n8cells_1_leftbaty_2, n8cells_1_rightbaty_2, n8cells_2_leftbaty_2, n8cells_2_rightbaty_2,
       n8cells_3_leftbaty_2, n8cells_3_rightbaty_2;

  _8cells u_8cells_1 (
    .chipID(chipID), .ballX(ballX), .ballY(ballY), .leftbatY(leftbatY), .rightbatY(rightbatY),
    .chipID_2(n8cells_1_chipid_2), .ballX_2(n8cells_1_ballx_2), .ballY_2(n8cells_1_bally_2),
    .leftbatY_2(n8cells_1_leftbaty_2), .rightbatY_2(n8cells_1_rightbaty_2), .out_6(out_6), .out_7(out_22),
    .out_8(out_7), .out_9(out_23), .out_10(out_8), .out_11(out_24), .out_12(out_9), .out_13(out_25));
  _8cells u_8cells_2 (
    .chipID(n8cells_1_chipid_2), .ballX(n8cells_1_ballx_2), .ballY(n8cells_1_bally_2),
    .leftbatY(n8cells_1_leftbaty_2), .rightbatY(n8cells_1_rightbaty_2), .chipID_2(n8cells_2_chipid_2),
    .ballX_2(n8cells_2_ballx_2), .ballY_2(n8cells_2_bally_2), .leftbatY_2(n8cells_2_leftbaty_2),
    .rightbatY_2(n8cells_2_rightbaty_2), .out_6(out_10), .out_7(out_26), .out_8(out_11), .out_9(out_27),
    .out_10(out_12), .out_11(out_28), .out_12(out_13), .out_13(out_29));
  _8cells u_8cells_3 (
    .chipID(n8cells_2_chipid_2), .ballX(n8cells_2_ballx_2), .ballY(n8cells_2_bally_2),
    .leftbatY(n8cells_2_leftbaty_2), .rightbatY(n8cells_2_rightbaty_2), .chipID_2(n8cells_3_chipid_2),
    .ballX_2(n8cells_3_ballx_2), .ballY_2(n8cells_3_bally_2), .leftbatY_2(n8cells_3_leftbaty_2),
    .rightbatY_2(n8cells_3_rightbaty_2), .out_6(out_14), .out_7(out_30), .out_8(out_15), .out_9(out_31),
    .out_10(out_16), .out_11(out_32), .out_12(out_17), .out_13(out_33));
  _8cells u_8cells_4 (
    .chipID(n8cells_3_chipid_2), .ballX(n8cells_3_ballx_2), .ballY(n8cells_3_bally_2),
    .leftbatY(n8cells_3_leftbaty_2), .rightbatY(n8cells_3_rightbaty_2), .out_6(out_18), .out_7(out_34),
    .out_8(out_19), .out_9(out_35), .out_10(out_20), .out_11(out_36), .out_12(out_21), .out_13(out_37));  // open: chipID_2, ballX_2, ballY_2, leftbatY_2, rightbatY_2
endmodule

module _8cells (
  input  [4:0] chipID,
  input  [4:0] ballX,
  input  [4:0] ballY,
  input  [31:0] leftbatY,
  input  [31:0] rightbatY,
  output [31:0] out_6,
  output [31:0] out_7,
  output [31:0] out_8,
  output [31:0] out_9,
  output [31:0] out_10,
  output [31:0] out_11,
  output [31:0] out_12,
  output [31:0] out_13,
  output [4:0] chipID_2,
  output [4:0] ballX_2,
  output [4:0] ballY_2,
  output [31:0] leftbatY_2,
  output [31:0] rightbatY_2
);

  wire [4:0] n1cell_1_out_7, n1cell_1_out_8, n1cell_1_out_9, n1cell_2_out_7, n1cell_2_out_8, n1cell_2_out_9,
       n1cell_3_out_7, n1cell_3_out_8, n1cell_3_out_9, n1cell_4_out_7, n1cell_4_out_8, n1cell_4_out_9,
       n1cell_5_out_7, n1cell_5_out_8, n1cell_5_out_9, n1cell_6_out_7, n1cell_6_out_8, n1cell_6_out_9,
       n1cell_7_out_7, n1cell_7_out_8, n1cell_7_out_9;
  wire [31:0] n1cell_1_out_10, n1cell_1_out_11, n1cell_2_out_10, n1cell_2_out_11, n1cell_3_out_10,
       n1cell_3_out_11, n1cell_4_out_10, n1cell_4_out_11, n1cell_5_out_10, n1cell_5_out_11, n1cell_6_out_10,
       n1cell_6_out_11, n1cell_7_out_10, n1cell_7_out_11;

  _1cell u_1cell_1 (
    .chipID(chipID), .ballX(ballX), .ballY(ballY), .leftbatY(leftbatY), .rightbatY(rightbatY),
    .out_7(n1cell_1_out_7), .out_8(n1cell_1_out_8), .out_9(n1cell_1_out_9), .out_10(n1cell_1_out_10),
    .out_11(n1cell_1_out_11), .out_6(out_6));
  _1cell u_1cell_2 (
    .chipID(n1cell_1_out_7), .ballX(n1cell_1_out_8), .ballY(n1cell_1_out_9), .leftbatY(n1cell_1_out_10),
    .rightbatY(n1cell_1_out_11), .out_7(n1cell_2_out_7), .out_8(n1cell_2_out_8), .out_9(n1cell_2_out_9),
    .out_10(n1cell_2_out_10), .out_11(n1cell_2_out_11), .out_6(out_7));
  _1cell u_1cell_3 (
    .chipID(n1cell_2_out_7), .ballX(n1cell_2_out_8), .ballY(n1cell_2_out_9), .leftbatY(n1cell_2_out_10),
    .rightbatY(n1cell_2_out_11), .out_7(n1cell_3_out_7), .out_8(n1cell_3_out_8), .out_9(n1cell_3_out_9),
    .out_10(n1cell_3_out_10), .out_11(n1cell_3_out_11), .out_6(out_8));
  _1cell u_1cell_4 (
    .chipID(n1cell_3_out_7), .ballX(n1cell_3_out_8), .ballY(n1cell_3_out_9), .leftbatY(n1cell_3_out_10),
    .rightbatY(n1cell_3_out_11), .out_7(n1cell_4_out_7), .out_8(n1cell_4_out_8), .out_9(n1cell_4_out_9),
    .out_10(n1cell_4_out_10), .out_11(n1cell_4_out_11), .out_6(out_9));
  _1cell u_1cell_5 (
    .chipID(n1cell_4_out_7), .ballX(n1cell_4_out_8), .ballY(n1cell_4_out_9), .leftbatY(n1cell_4_out_10),
    .rightbatY(n1cell_4_out_11), .out_7(n1cell_5_out_7), .out_8(n1cell_5_out_8), .out_9(n1cell_5_out_9),
    .out_10(n1cell_5_out_10), .out_11(n1cell_5_out_11), .out_6(out_10));
  _1cell u_1cell_6 (
    .chipID(n1cell_5_out_7), .ballX(n1cell_5_out_8), .ballY(n1cell_5_out_9), .leftbatY(n1cell_5_out_10),
    .rightbatY(n1cell_5_out_11), .out_7(n1cell_6_out_7), .out_8(n1cell_6_out_8), .out_9(n1cell_6_out_9),
    .out_10(n1cell_6_out_10), .out_11(n1cell_6_out_11), .out_6(out_11));
  _1cell u_1cell_7 (
    .chipID(n1cell_6_out_7), .ballX(n1cell_6_out_8), .ballY(n1cell_6_out_9), .leftbatY(n1cell_6_out_10),
    .rightbatY(n1cell_6_out_11), .out_7(n1cell_7_out_7), .out_8(n1cell_7_out_8), .out_9(n1cell_7_out_9),
    .out_10(n1cell_7_out_10), .out_11(n1cell_7_out_11), .out_6(out_12));
  _1cell u_1cell_8 (
    .chipID(n1cell_7_out_7), .ballX(n1cell_7_out_8), .ballY(n1cell_7_out_9), .leftbatY(n1cell_7_out_10),
    .rightbatY(n1cell_7_out_11), .out_7(chipID_2), .out_8(ballX_2), .out_9(ballY_2), .out_10(leftbatY_2),
    .out_11(rightbatY_2), .out_6(out_13));
endmodule

module _1cell (
  input  [4:0] chipID,
  input  [4:0] ballX,
  input  [4:0] ballY,
  input  [31:0] leftbatY,
  input  [31:0] rightbatY,
  output [31:0] out_6,
  output [4:0] out_7,
  output [4:0] out_8,
  output [4:0] out_9,
  output [31:0] out_10,
  output [31:0] out_11
);

  wire comparator_1_eq, comparator_1_gt, comparator_1_lt, comparator_2_eq, comparator_2_gt, comparator_2_lt,
       comparator_3_eq, comparator_3_gt, comparator_3_lt, or_1_out, or_2_out;
  wire [31:0] ball, decoder_1_out0, lbat_t, rbat_t;

  // Probe on 5'b00011
  // Probe on 5'b11100
  // Probe on leftbatY
  Comparator #(.width(5)) comparator_1 (
    .a(chipID), .b(ballX), .gt(comparator_1_gt), .eq(comparator_1_eq), .lt(comparator_1_lt));
  Comparator #(.width(5)) comparator_2 (
    .a(chipID), .b(5'b00011), .gt(comparator_2_gt), .eq(comparator_2_eq), .lt(comparator_2_lt));
  or or_1 (or_1_out, comparator_2_lt, comparator_2_gt);
  Comparator #(.width(5)) comparator_3 (
    .a(chipID), .b(5'b11100), .gt(comparator_3_gt), .eq(comparator_3_eq), .lt(comparator_3_lt));
  or or_2 (or_2_out, comparator_3_lt, comparator_3_gt);
  assign out_6 = rbat_t | lbat_t | ball;  // OR_Gate or_3, 32 bits wide
  Decoder #(.select(5)) decoder_1 (
    .out0(decoder_1_out0[0]), .out1(decoder_1_out0[1]), .out2(decoder_1_out0[2]), .out3(decoder_1_out0[3]),
    .out4(decoder_1_out0[4]), .out5(decoder_1_out0[5]), .out6(decoder_1_out0[6]), .out7(decoder_1_out0[7]),
    .out8(decoder_1_out0[8]), .out9(decoder_1_out0[9]), .out10(decoder_1_out0[10]),
    .out11(decoder_1_out0[11]), .out12(decoder_1_out0[12]), .out13(decoder_1_out0[13]),
    .out14(decoder_1_out0[14]), .out15(decoder_1_out0[15]), .out16(decoder_1_out0[16]),
    .out17(decoder_1_out0[17]), .out18(decoder_1_out0[18]), .out19(decoder_1_out0[19]),
    .out20(decoder_1_out0[20]), .out21(decoder_1_out0[21]), .out22(decoder_1_out0[22]),
    .out23(decoder_1_out0[23]), .out24(decoder_1_out0[24]), .out25(decoder_1_out0[25]),
    .out26(decoder_1_out0[26]), .out27(decoder_1_out0[27]), .out28(decoder_1_out0[28]),
    .out29(decoder_1_out0[29]), .out30(decoder_1_out0[30]), .out31(decoder_1_out0[31]), .sel(ballY),
    .en(comparator_1_eq));
  // Probe on ball
  Multiplexer #(.width(32), .enable("false")) multiplexer_1 (
    .in0({32{1'b0}}), .in1(decoder_1_out0), .out(ball), .sel(comparator_1_eq));
  Transistor #(.\type ("n"), .width(32)) transistor_1 (.in(leftbatY), .out(lbat_t), .gate(comparator_2_eq));
  Transistor #(.\type ("n"), .gate("br"), .width(32)) transistor_2 (.in({32{1'b0}}), .out(lbat_t), .gate(or_1_out));
  Transistor #(.\type ("n"), .width(32)) transistor_3 (.in(rightbatY), .out(rbat_t), .gate(comparator_3_eq));
  Transistor #(.\type ("n"), .gate("br"), .width(32)) transistor_4 (.in({32{1'b0}}), .out(rbat_t), .gate(or_2_out));
  // Probe on lbat_t
  // Probe on rbat_t
  Adder #(.width(5)) adder_1 (.a(5'b00001), .b(chipID), .out(out_7));  // open: cin, cout

  assign out_8 = ballX;
  assign out_9 = ballY;
  assign out_10 = leftbatY;
  assign out_11 = rightbatY;
endmodule

module kinematic_controller (
  input  down,
  input  up,
  input  [1:0] joystick,
  input  reset,
  input  [4:0] ballX,
  input  [4:0] ballY,
  input  [4:0] rightBat,
  input  [7:0] velocity,
  input  [3:0] Rscores,
  input  clock,
  input  [3:0] Lscores,
  output [4:0] chipID,
  output [4:0] ballX_2,
  output [4:0] ballY_2,
  output [31:0] leftbatY,
  output [31:0] rightbatY
);

  wire and_1_out, and_2_out, and_3_out, button_1_out, button_2_out, comparator_1_eq, comparator_2_eq,
       or_1_out, or_2_out;
  wire [4:0] adder_1_out, adder_2_out, register_2_q;
  wire [4:4] and_4_out;
  wire [31:0] decoder_1_out0, decoder_2_out0, shifter_1_out, shifter_2_out, shifter_3_out, shifter_4_out;

  Register register_1 (.en(clock));  // open: D, Q, clk, clr
  // Probe on joystick
  Button button_1 (.out(button_1_out));
  Button button_2 (.out(button_2_out));
  and and_1 (and_1_out, ~joystick[1], joystick[0]);  // AND_Gate
  or or_1 (or_1_out, and_1_out, button_2_out);
  or or_2 (or_2_out, button_1_out, and_2_out);
  and and_2 (and_2_out, joystick[1], joystick[0]);
  and and_3 (and_3_out, ~comparator_1_eq, or_1_out, ~and_4_out[4]);  // AND_Gate
  and and_4 (and_4_out[4], ~and_3_out, or_2_out, ~comparator_2_eq);  // AND_Gate
  // Probe on register_2_q
  Adder #(.width(5)) adder_1 (
    .a(register_2_q), .b({5{and_4_out[4]}}), .out(adder_1_out), .cin(and_3_out));  // open: cout
  Register #(.width(5)) register_2 (.D(adder_1_out), .Q(register_2_q), .clk(clock));  // open: en, clr
  Adder #(.width(5)) adder_2 (.a(register_2_q), .b(5'b01111), .out(adder_2_out));  // open: cin, cout
  // Probe on adder_2_out
  Comparator #(.width(5), .mode("unsigned")) comparator_1 (
    .a(5'b11101), .b(adder_2_out), .eq(comparator_1_eq));  // open: gt, lt
  Comparator #(.width(5), .mode("unsigned")) comparator_2 (
    .a(adder_2_out), .b({5{1'b0}}), .eq(comparator_2_eq));  // open: gt, lt
  Decoder #(.select(5), .enable("false")) decoder_1 (
    .out0(decoder_1_out0[0]), .out1(decoder_1_out0[1]), .out2(decoder_1_out0[2]), .out3(decoder_1_out0[3]),
    .out4(decoder_1_out0[4]), .out5(decoder_1_out0[5]), .out6(decoder_1_out0[6]), .out7(decoder_1_out0[7]),
    .out8(decoder_1_out0[8]), .out9(decoder_1_out0[9]), .out10(decoder_1_out0[10]),
    .out11(decoder_1_out0[11]), .out12(decoder_1_out0[12]), .out13(decoder_1_out0[13]),
    .out14(decoder_1_out0[14]), .out15(decoder_1_out0[15]), .out16(decoder_1_out0[16]),
    .out17(decoder_1_out0[17]), .out18(decoder_1_out0[18]), .out19(decoder_1_out0[19]),
    .out20(decoder_1_out0[20]), .out21(decoder_1_out0[21]), .out22(decoder_1_out0[22]),
    .out23(decoder_1_out0[23]), .out24(decoder_1_out0[24]), .out25(decoder_1_out0[25]),
    .out26(decoder_1_out0[26]), .out27(decoder_1_out0[27]), .out28(decoder_1_out0[28]),
    .out29(decoder_1_out0[29]), .out30(decoder_1_out0[30]), .out31(decoder_1_out0[31]), .sel(adder_2_out));
  Decoder #(.select(5), .enable("false")) decoder_2 (
    .out0(decoder_2_out0[0]), .out1(decoder_2_out0[1]), .out2(decoder_2_out0[2]), .out3(decoder_2_out0[3]),
    .out4(decoder_2_out0[4]), .out5(decoder_2_out0[5]), .out6(decoder_2_out0[6]), .out7(decoder_2_out0[7]),
    .out8(decoder_2_out0[8]), .out9(decoder_2_out0[9]), .out10(decoder_2_out0[10]),
    .out11(decoder_2_out0[11]), .out12(decoder_2_out0[12]), .out13(decoder_2_out0[13]),
    .out14(decoder_2_out0[14]), .out15(decoder_2_out0[15]), .out16(decoder_2_out0[16]),
    .out17(decoder_2_out0[17]), .out18(decoder_2_out0[18]), .out19(decoder_2_out0[19]),
    .out20(decoder_2_out0[20]), .out21(decoder_2_out0[21]), .out22(decoder_2_out0[22]),
    .out23(decoder_2_out0[23]), .out24(decoder_2_out0[24]), .out25(decoder_2_out0[25]),
    .out26(decoder_2_out0[26]), .out27(decoder_2_out0[27]), .out28(decoder_2_out0[28]),
    .out29(decoder_2_out0[29]), .out30(decoder_2_out0[30]), .out31(decoder_2_out0[31]), .sel(rightBat));
  // Probe on decoder_1_out0
  // Probe on decoder_2_out0
  Shifter #(.width(32)) shifter_1 (.in(decoder_1_out0), .\dist (5'b00001), .out(shifter_1_out));
  Shifter #(.width(32)) shifter_2 (.in(decoder_2_out0), .\dist (5'b00001), .out(shifter_2_out));
  Shifter #(.width(32)) shifter_3 (.in(shifter_1_out), .\dist (5'b00001), .out(shifter_3_out));
  Shifter #(.width(32)) shifter_4 (.in(shifter_2_out), .\dist (5'b00001), .out(shifter_4_out));
  assign leftbatY = decoder_1_out0 | shifter_1_out | shifter_3_out;  // OR_Gate or_3, 32 bits wide
  assign rightbatY = decoder_2_out0 | shifter_2_out | shifter_4_out;  // OR_Gate or_4, 32 bits wide
  // Probe on leftbatY
  // Probe on rightbatY

  assign ballX_2 = ballX;
  assign ballY_2 = ballY;
  assign chipID = {5{1'b0}};

  // Other names for the same wires on the sheet: batRes = reset; clk = clock; lBat[31:0] = leftbatY;
  //   rBat[31:0] = rightbatY; rBatIn[4:0] = rightBat
endmodule

module hit_detection (
  input  [31:0] bat,
  input  coll,
  input  [31:0] ballY,
  output hit
);

  wire or_1_out;
  wire [31:0] and_1_out;

  assign and_1_out = bat & ballY;  // AND_Gate and_1, 32 bits wide
  or or_1 (or_1_out, and_1_out[0], and_1_out[1], and_1_out[2], and_1_out[3], and_1_out[4], and_1_out[5], and_1_out[6], and_1_out[7], and_1_out[8], and_1_out[9], and_1_out[10], and_1_out[11], and_1_out[12], and_1_out[13], and_1_out[14], and_1_out[15], and_1_out[16], and_1_out[17], and_1_out[18], and_1_out[19], and_1_out[20], and_1_out[21], and_1_out[22], and_1_out[23], and_1_out[24], and_1_out[25], and_1_out[26], and_1_out[27], and_1_out[28], and_1_out[29], and_1_out[30], and_1_out[31]);
  and and_2 (hit, or_1_out, coll);
endmodule
